# Fritzing sketch sketch (saved by Fritzing 0.9.3b)
breadboards: 1

parts:
  Part1 = Spark Core (v1.0)
  U1 = 8RelayModule

nets:
  N1: Part1.A0, U1.IN5
  N2: Part1.A1, U1.IN6
  N3: Part1.A2, U1.IN7
  N4: Part1.A3, U1.IN8
  GND: Part1.GND, U1.GND
  VIN: Part1.VIN, U1.VCC
  N5: Part1.D1, U1.IN1
  N6: Part1.D2, U1.IN2
  N7: Part1.D3, U1.IN3
  N8: Part1.D4, U1.IN4

custom parts:
  8RelayModule: 8 relay arduino module SONGLE SRD05VDC-SL-C
